// Logisim project subleq.circ as structural Verilog: 1 circuit, main circuit main
module main (
  input  [7:0] A,
  input  [7:0] B,
  input  [7:0] C,
  output [7:0] out_4
);

  wire button_1_out, clock_1_out, controlled_buffer_1_out, Reset_out, t_ff_1_q;
  wire [7:0] register_1_q, register_2_q, register_4_q;

  Button Reset (.out(Reset_out));
  T_Flip_Flop t_ff_1 (.T(button_1_out), .clk(button_1_out), .Q(t_ff_1_q));  // open: Qn, reset, preset
  Button button_1 (.out(button_1_out));
  Clock clock_1 (.out(clock_1_out));
  assign controlled_buffer_1_out = t_ff_1_q ? clock_1_out : 1'bz;  // Controlled_Buffer controlled_buffer_1
  Register register_1 (
    .D(A), .en(controlled_buffer_1_out), .clk(controlled_buffer_1_out), .Q(register_1_q), .clr(Reset_out));
  Register register_2 (
    .D(B), .en(controlled_buffer_1_out), .clk(controlled_buffer_1_out), .Q(register_2_q), .clr(Reset_out));
  Register register_3 (
    .D(B), .en(controlled_buffer_1_out), .clk(controlled_buffer_1_out), .Q(register_2_q), .clr(Reset_out));
  Register register_4 (
    .D(C), .en(controlled_buffer_1_out), .clk(controlled_buffer_1_out), .Q(register_4_q), .clr(Reset_out));
  Register register_5 (
    .D(C), .en(controlled_buffer_1_out), .clk(controlled_buffer_1_out), .Q(register_4_q), .clr(Reset_out));
  Pull_Resistor pull_resistor_1 (.node(controlled_buffer_1_out));
  Subtractor subtractor_1 (.a(register_1_q), .b(register_2_q), .out(out_4));  // open: bin, bout
endmodule
